// Logisim project ProyectoFinal.circ as structural Verilog: 4 circuits, main circuit main
module main (
  input  S2,
  input  S1,
  input  S0,
  input  M,
  input  E,
  input  Ta,
  input  Tb,
  output S22,
  output S11,
  output S00
);

  wire and_1_out, and_2_out, and_3_out, and_4_out, and_5_out, and_6_out, and_7_out, not_1_out, not_2_out,
       not_3_out, not_4_out, not_5_out, not_6_out, not_7_out, not_8_out, not_9_out, not_10_out, not_11_out,
       not_12_out, not_13_out, not_14_out, not_15_out, not_16_out, not_17_out, not_18_out, not_19_out,
       not_20_out, not_21_out, not_22_out, not_23_out, not_24_out, not_25_out, not_26_out, not_27_out;

  not not_1 (not_1_out, S2);
  not not_2 (not_2_out, S1);
  not not_3 (not_3_out, S0);
  not not_4 (not_4_out, S2);
  not not_5 (not_5_out, S1);
  not not_6 (not_6_out, M);
  not not_7 (not_7_out, E);
  not not_8 (not_8_out, S2);
  not not_9 (not_9_out, S1);
  not not_10 (not_10_out, M);
  not not_11 (not_11_out, Ta);
  not not_12 (not_12_out, Tb);
  not not_13 (not_13_out, S2);
  not not_14 (not_14_out, S0);
  not not_15 (not_15_out, M);
  not not_16 (not_16_out, E);
  not not_17 (not_17_out, S2);
  not not_18 (not_18_out, S1);
  not not_19 (not_19_out, S0);
  not not_20 (not_20_out, M);
  not not_21 (not_21_out, E);
  not not_22 (not_22_out, Ta);
  not not_23 (not_23_out, S2);
  not not_24 (not_24_out, S0);
  not not_25 (not_25_out, M);
  not not_26 (not_26_out, E);
  not not_27 (not_27_out, Tb);
  and and_1 (and_1_out, not_1_out, M);
  and and_2 (and_2_out, not_2_out, not_3_out, M);
  and and_3 (and_3_out, not_4_out, not_5_out, S0, not_6_out, not_7_out);
  and and_4 (and_4_out, not_8_out, not_9_out, S0, not_10_out, not_11_out, not_12_out);
  and and_5 (and_5_out, not_13_out, S1, not_14_out, not_15_out, not_16_out);
  and and_6 (and_6_out, not_17_out, not_18_out, not_19_out, not_20_out, not_21_out, not_22_out);
  and and_7 (and_7_out, not_23_out, S1, not_24_out, not_25_out, not_26_out, not_27_out);
  or or_1 (S22, and_1_out, and_2_out);
  or or_2 (S11, and_3_out, and_4_out, and_5_out);
  or or_3 (S00, and_6_out, and_7_out);
endmodule

module main2 (
  input  B1,
  input  B1_2,
  input  B1_3,
  input  B1_4
);

  wire clock_1_out, d_ff_1_q, d_ff_2_q, d_ff_3_q, decoder_1_g, decoder_1_r, decoder_1_y, decoder_2_g,
       decoder_2_r, decoder_2_y, main_1_s00, main_1_s11, main_1_s22, output_logic_1_la0, output_logic_1_la1,
       output_logic_1_lb0, output_logic_1_lb1, undriven, undriven_2, undriven_3, undriven_4, undriven_5,
       undriven_6, undriven_7;

  main main_1 (
    .S2(d_ff_1_q), .S1(d_ff_2_q), .S0(d_ff_3_q), .M(B1), .E(B1_2), .Ta(B1_3), .Tb(B1_4), .S22(main_1_s22),
    .S11(main_1_s11), .S00(main_1_s00));
  Clock clock_1 (.out(clock_1_out));
  D_Flip_Flop d_ff_1 (.clk(clock_1_out), .D(main_1_s22), .Q(d_ff_1_q));  // open: Qn, preset, en, reset
  D_Flip_Flop d_ff_2 (.clk(clock_1_out), .D(main_1_s11), .Q(d_ff_2_q));  // open: Qn, preset, en, reset
  D_Flip_Flop d_ff_3 (.clk(clock_1_out), .D(main_1_s00), .Q(d_ff_3_q));  // open: Qn, preset, en, reset
  output_logic output_logic_1 (
    .S2(d_ff_1_q), .S1(d_ff_2_q), .S0(d_ff_3_q), .LA1(output_logic_1_la1), .LA0(output_logic_1_la0),
    .LB1(output_logic_1_lb1), .LB0(output_logic_1_lb0));
  LED led_1 (.in(decoder_1_r));
  LED led_2 (.in(decoder_1_y));
  decoder decoder_1 (
    .l1(output_logic_1_la1), .l0(output_logic_1_la0), .R(decoder_1_r), .G(decoder_1_g), .Y(decoder_1_y));
  LED led_3 (.in(decoder_1_g));
  LED led_4 (.in(decoder_2_r));
  decoder decoder_2 (
    .l1(output_logic_1_lb1), .l0(output_logic_1_lb0), .R(decoder_2_r), .G(decoder_2_g), .Y(decoder_2_y));
  LED led_5 (.in(decoder_2_y));
  LED led_6 (.in(decoder_2_g));
  LED led_7 ();  // open: in
  LED led_8 ();  // open: in
  LED led_9 ();  // open: in
  LED led_10 ();  // open: in
  LED led_11 (.in(undriven_3));
  LED led_12 (.in(undriven_3));
  LED led_13 (.in(undriven_3));
  LED led_14 (.in(undriven_3));
  LED led_15 (.in(undriven_3));
  LED led_16 ();  // open: in
  LED led_17 ();  // open: in
  LED led_18 ();  // open: in
  LED led_19 ();  // open: in
  LED led_20 (.in(undriven_4));
  LED led_21 ();  // open: in
  LED led_22 (.in(undriven_4));
  LED led_23 (.in(undriven_4));
  LED led_24 (.in(undriven_4));
  LED led_25 (.in(undriven_4));
  LED led_26 ();  // open: in
  LED led_27 ();  // open: in
  LED led_28 ();  // open: in
  LED led_29 ();  // open: in
  LED led_30 (.in(undriven));
  LED led_31 (.in(undriven));
  LED led_32 ();  // open: in
  LED led_33 (.in(undriven));
  LED led_34 (.in(undriven));
  LED led_35 (.in(undriven));
  LED led_36 ();  // open: in
  LED led_37 ();  // open: in
  LED led_38 ();  // open: in
  LED led_39 ();  // open: in
  LED led_40 (.in(undriven_5));
  LED led_41 (.in(undriven_5));
  LED led_42 (.in(undriven_5));
  LED led_43 ();  // open: in
  LED led_44 ();  // open: in
  LED led_45 ();  // open: in
  LED led_46 (.in(undriven_7));
  LED led_47 (.in(undriven_7));
  LED led_48 (.in(undriven_7));
  LED led_49 (.in(undriven_6));
  LED led_50 (.in(undriven_6));
  LED led_51 (.in(undriven_6));
  LED led_52 (.in(undriven_2));
  LED led_53 (.in(undriven_2));
  LED led_54 (.in(undriven_2));

  // Notes on the sheet:
  //   EAST
  //   EAST
  //   EAST
  //   WEST
  //   WEST
  //   WEST
  //   North
  //   North
  //   North
endmodule

module output_logic (
  input  S2,
  input  S1,
  input  S0,
  output LA1,
  output LA0,
  output LB1,
  output LB0
);

  wire and_1_out, and_2_out, and_4_out, and_5_out, not_1_out, not_2_out, not_3_out, not_4_out, not_5_out,
       not_6_out, not_7_out, not_8_out, not_9_out, not_10_out;

  not not_1 (not_1_out, S2);
  not not_2 (not_2_out, S1);
  not not_3 (not_3_out, S0);
  not not_4 (not_4_out, S2);
  not not_5 (not_5_out, S1);
  not not_6 (not_6_out, S2);
  not not_7 (not_7_out, S1);
  not not_8 (not_8_out, S1);
  not not_9 (not_9_out, S0);
  not not_10 (not_10_out, S2);
  and and_1 (and_1_out, not_1_out, S1);
  and and_2 (and_2_out, S2, not_2_out, not_3_out);
  and and_3 (LA0, not_4_out, not_5_out, S0);
  and and_4 (and_4_out, not_6_out, not_7_out);
  and and_5 (and_5_out, not_8_out, not_9_out);
  and and_6 (LB0, not_10_out, S1, S0);
  or or_1 (LA1, and_1_out, and_2_out);
  or or_2 (LB1, and_4_out, and_5_out);
endmodule

module decoder (
  input  l1,
  input  l0,
  output R,
  output G,
  output Y
);

  wire not_1_out, not_2_out, not_3_out, not_4_out;

  not not_1 (not_1_out, l0);
  not not_2 (not_2_out, l1);
  not not_3 (not_3_out, l0);
  not not_4 (not_4_out, l1);
  and and_1 (R, l1, not_1_out);
  and and_2 (G, not_2_out, not_3_out);
  and and_3 (Y, not_4_out, l0);
endmodule
